// Logisim project cpu.circ as structural Verilog: 1 circuit, main circuit cpu
module cpu (
  input  clk,
  input  [31:0] INSTRUCTION,
  input  [31:0] READ_DATA,
  output [31:0] WRITE_ADDRESS,
  output [31:0] PROGRAM_COUNTER,
  output [31:0] ra,
  output [31:0] sp,
  output [31:0] t0,
  output [31:0] t1,
  output [31:0] t2,
  output [31:0] s0,
  output [31:0] s1,
  output [31:0] a0,
  output [31:0] tohost,
  output [3:0] WRITE_ENABLE,
  output [31:0] WRITE_DATA,
  output [31:0] out_17,
  output [31:0] out_18,
  output [6:0] out_19,
  output [4:0] out_20,
  output [31:0] out_21,
  output [4:0] out_22,
  output [2:0] out_23,
  output [4:0] out_24
);

  wire ASel, BrEq, BrLt, BrUn, BSel, CSRSel, CSRWen, MemRW, PCSel, RegWEn;
  wire [1:0] WBSel;
  wire [2:0] ImmSel;
  wire [3:0] ALUSel, bit_extender_1_out, multiplexer_3_out;
  wire [31:0] adder_1_out, adder_2_out, bit_extender_2_out, multiplexer_1_out, multiplexer_2_out,
       multiplexer_4_out, multiplexer_5_out, multiplexer_6_out, pcEX, read_data_1;
  wire [31:25] instEX;

  Adder #(.width(32)) adder_1 (.a(PROGRAM_COUNTER), .b(32'h4), .out(adder_1_out));  // open: cin, cout
  Register #(.width(32)) PC (.D(multiplexer_1_out), .clk(clk), .Q(PROGRAM_COUNTER));  // open: en, clr
  Multiplexer #(.enable("false"), .width(32)) multiplexer_1 (
    .in0(adder_1_out), .in1(out_18), .out(multiplexer_1_out), .sel(PCSel));
  Multiplexer #(.enable("false"), .width(32)) multiplexer_2 (
    .in0(INSTRUCTION), .in1(32'h13), .out(multiplexer_2_out), .sel(PCSel));
  Register #(.width(32)) u_instEX (
    .D(multiplexer_2_out), .clk(clk), .Q({instEX, out_22, out_20, out_23, out_24, out_19}));  // open: en, clr
  Register #(.width(32)) u_pcEX (.D(PROGRAM_COUNTER), .clk(clk), .Q(pcEX));  // open: en, clr
  assign bit_extender_1_out = {{3{MemRW}}, MemRW};  // Bit_Extender bit_extender_1
  Multiplexer #(.enable("false"), .select(2), .width(4)) multiplexer_3 (
    .in0(4'b0001), .in1(4'b0011), .in2(4'b1111), .out(multiplexer_3_out), .sel(out_23[1:0]));  // open: in3
  control_logic control_logic_1 (
    .CSRWen(CSRWen), .PCSel(PCSel), .RegWEn(RegWEn), .ImmSel(ImmSel), .BrUn(BrUn), .ASel(ASel), .BSel(BSel),
    .ALUSel(ALUSel), .MemRW(MemRW), .WBSel(WBSel), .CSRSel(CSRSel),
    .inst({instEX, out_22, out_20, out_23, out_24, out_19}), .BrEq(BrEq), .BrLt(BrLt));
  assign WRITE_ENABLE = bit_extender_1_out & multiplexer_3_out;  // AND_Gate and_1, 4 bits wide
  imm_gen imm_gen_1 (.inst({instEX, out_22, out_20, out_23, out_24, out_19}), .ImmSel(ImmSel), .imm(out_17));
  regfile regfile_1 (
    .rs1(out_20), .rs2(out_22), .rd(out_24), .Write_Data(out_21), .RegWEn(RegWEn), .clk(clk), .ra(ra),
    .sp(sp), .t0(t0), .t1(t1), .t2(t2), .s0(s0), .s1(s1), .a0(a0), .Read_Data_1(read_data_1),
    .Read_Data_2(WRITE_DATA));
  branch_comp branch_comp_1 (.rs1(read_data_1), .rs2(WRITE_DATA), .BrUn(BrUn), .BrEq(BrEq), .BrLt(BrLt));
  Multiplexer #(.enable("false"), .width(32)) multiplexer_4 (
    .in0(read_data_1), .in1(pcEX), .out(multiplexer_4_out), .sel(ASel));
  Multiplexer #(.enable("false"), .width(32)) multiplexer_5 (
    .in0(WRITE_DATA), .in1(out_17), .out(multiplexer_5_out), .sel(BSel));
  assign bit_extender_2_out = {{27{1'b0}}, out_20};  // Bit_Extender bit_extender_2
  Multiplexer #(.enable("false"), .width(32)) multiplexer_6 (
    .in0(read_data_1), .in1(bit_extender_2_out), .out(multiplexer_6_out), .sel(CSRSel));
  alu alu_1 (.Result(out_18), .A(multiplexer_4_out), .B(multiplexer_5_out), .ALUSel(ALUSel));
  Adder #(.width(32)) adder_2 (.a(pcEX), .b(32'h4), .out(adder_2_out));  // open: cin, cout
  csr csr_1 (.CSR_address(out_18[11:0]), .CSR_din(multiplexer_6_out), .CSR_WE(CSRWen), .clk(clk), .tohost(tohost));
  Multiplexer #(.enable("false"), .select(2), .width(32)) multiplexer_7 (
    .in0(READ_DATA), .in1(out_18), .in2(adder_2_out), .out(out_21), .sel(WBSel));  // open: in3

  assign WRITE_ADDRESS = out_18;

  // Other names for the same wires on the sheet: alu_result[31:0] = out_18; imm[31:0] = out_17;
  //   instEX[24:0] = {out_22, out_20, out_23, out_24, out_19}; Opcode[6:0] = out_19; rd[4:0] = out_24;
  //   funct3[2:0] = out_23; rs1[4:0] = out_20; rs2[4:0] = out_22; read_data_2[31:0] = WRITE_DATA;
  //   reg_write_data[31:0] = out_21

  // Notes on the sheet:
  //   Output to IMEM
  //   IMEM (do **NOT** move this)
  //   Inputs from IMEM
  //   It is OK to move the PC, RegFile, ALU, MEM, Branch Comp, Imm Gen, and Control Logic to wherever is most convenient for you when constructing your CPU, and to delete this text
  //   Inputs/Outputs for testing. Do **NOT** move these.
  //   Outputs To DMEM
  //   DMEM (do **NOT** move this)
  //   Inputs From DMEM
endmodule
